# Fritzing sketch GoPro Timelapse (saved by Fritzing 0.9.3b)
breadboards: 1

parts:
  Part1 = Arduino Uno (Rev3)
  Part2 = Bluetooth HC-05 Macho
  LED1 = smd LED [color="Red (633nm)" package="0805 [SMD]"]
  R1 = Resistor [tolerance=±5% resistance=220 package="2010 [SMD]"]

nets:
  N1: Part1.D10_PWM/SS, Part2.TXD
  N2: Part1.D11_PWM/MOSI, Part2.RXD
  N3: Part1.D12/MISO, R1.Pin_0
  5V: Part1.5V, Part2.VCC
  GND: Part1.GND, Part2.GND
  N4: LED1.cathode, R1.Pin_1

// code stored in the sketch: Untitled2.ino

